# Fritzing sketch scheme (saved by Fritzing 0.9.3b)
breadboards: 1

parts:
  U1 = NodeMCU V1.0
  IC1 = MCP23017 I2C I/O Expander  # not connected
  U2 = 4-Channel 5v Relay Shield [package=relay-4ch5v10a]
  S1 = Pushbutton [package="[SMD]"]
  U3 = TLP621 [package=THT]
  R1 = Resistor [tolerance=±5% resistance=100 package="2512 [SMD]"]

nets:
  N1: U1.SD0, U2.VCC, U3.Pin_1
  N2: U2.GND, S1.Pin_1, S1.Pin_2, S1.Pin_3, S1.Pin_4, U3.Pin_3, R1.Pin_1
  N3: U3.Pin_2, R1.Pin_0

notes:
  to DHT22 module DAT

custom parts:
  NodeMCU V1.0: ESP8266 based NodeMCU
  MCP23017 I2C I/O Expander: The MCP23017 uses two i2c pins (these can be shared with other i2c devices), and in exchange gives you 16 general purpose pins. You can set each of 16 pins to be input, output, input with a pullup or open drain. There's even the ability to get an interrupt via an external pin when any of the inputs change so you don't have to keep polling the chip.
  4-Channel 5v Relay Shield: 4 Channel 5v Relay Shield w. 2x SPD-06VDC-SD-C
